# Fritzing sketch circuit (saved by Fritzing 0.9.3b)
circuit board: 8.46667cm x 5.64444cm

parts:
  L298N1 = L298N DC motor driver
  M1 = DC Motor
  M2 = DC Motor
  Part1 = Arduino Nano (Rev3.0)
  GY2 = MPU-6050 Board GY-521 [form="♀ (female)" package=THT]
  S1 = Toggle Switch spst [package=THT]
  Part2 = Bluetooth HC-05
  BAT1 = BC9VPC [package=bc9vpc]

nets:
  N1: L298N1.OUT1, M2.pin_2
  N2: L298N1.OUT2, M2.pin_1
  N3: L298N1.OUT3, M1.pin_2
  N4: L298N1.OUT4, M1.pin_1
  N5: L298N1.12V, BAT1.V+
  N6: L298N1.GND, S1.COM
  5V: L298N1.5V, Part1.VIN
  N7: L298N1.ENA, Part1.D5
  N8: L298N1.ENB, Part1.D10
  N9: L298N1.IN1, Part1.D6
  N10: L298N1.IN2, Part1.D7
  N11: L298N1.IN3, Part1.D8
  N12: L298N1.IN4, Part1.D9
  N13: Part1.D1/TX, Part2.RXD
  N14: Part1.D0/RX, Part2.TXD
  N15: Part1.GND, GY2.pin2
  5V_2: Part1.5V, Part2.VCC
  N16: Part1.A5, GY2.pin4
  N17: Part1.A4, GY2.pin3
  N18: Part1.3V3, GY2.pin1
  N19: S1.L1, BAT1.V-

custom parts:
  L298N DC motor driver: 2x DC motor driver with 78M05 positive voltage regulator (7..35 V) L298N: max 46 V, 2 A Set 5 V Enable jumper to enable 5 V regultor (needed for the L298N) and +5 V output at screw terminal or supply external +5 V at screw terminal Set ENA and/or ENB to +5 V to enable motor permanently or supply ENA and/or ENB with PWM signal IN1 and IN2 set rotation directory for motor A (OUT1/OUT2) IN2 and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
  MPU-6050 Board GY-521: Acelerometro y Giroscopio MPU-6050 Board GY-521
  Toggle Switch spst: Toggle Switch single pole single throw
